# Fritzing sketch diagrama (saved by Fritzing 0.9.3b)

parts:
  VCC1 = Battery block 9V
  Componente1 = Arduino Nano (Rev3.0)
  U1 = SWITCH-SPST-2 [package=switch-spst-vertical]

nets:
  N1: VCC1.-, Componente1.GND
  N2: VCC1.+, U1.O
  N3: Componente1.VIN, U1.P
