# Fritzing sketch diagrama_conexion (saved by Fritzing 0.9.3b)

parts:
  S1 = H-Bridge with L298N
  VCC1 = Battery block 9V
  M1 = DC Motor
  M3 = DC Motor
  M4 = DC Motor
  Componente1 = Arduino Nano (Rev3.0)
  M2 = DC Motor

nets:
  N1: S1.12V, VCC1.+
  GND: S1.GND, VCC1.-, Componente1.GND
  5V: S1.5V, Componente1.5V
  N2: S1.ENA, Componente1.D11/MOSI
  N3: S1.IN1, Componente1.D10
  N4: S1.IN2, Componente1.D9
  N5: S1.IN3, Componente1.D8
  N6: S1.IN4, Componente1.D7
  N7: S1.ENB, Componente1.D6
  N8: S1.M1-01, M3.pin_2, M4.pin_2
  N9: S1.M1-02, M3.pin_1, M4.pin_1
  N10: S1.M2-01, M1.pin_1, M2.pin_1
  N11: S1.M2-02, M1.pin_2, M2.pin_2

custom parts:
  H-Bridge with L298N: h-bridge
