# Fritzing sketch diagrama_de_conexion (saved by Fritzing 0.9.3b)
breadboards: 1

parts:
  M1 = fc-51 [package=THT]
  R1 = Resistor [tolerance=±5% resistance=220 package=THT]
  LED1 = LED - 5mm [color="Red (633nm)" package="5 mm [THT]"]
  Componente1 = Arduino Uno (Rev3)
  S1 = Pushbutton [package="[THT]"]
  R2 = Resistor [tolerance=±5% resistance=220 package=THT]

nets:
  N1: M1.pin1, Componente1.D2
  N2: M1.pin2, Componente1.GND, R2.Pin_0
  N3: M1.pin3, Componente1.5V, S1.Pin_1, S1.Pin_2
  N4: R1.Pin_1, LED1.cathode
  N5: LED1.anode, Componente1.D12/MISO
  N6: Componente1.D7, S1.Pin_3, S1.Pin_4, R2.Pin_1
