# Fritzing sketch fc-28 humedad de suelo (saved by Fritzing 0.9.3b)
breadboards: 1

parts:
  Componente1 = FC-28 Soil Hygrometer Module - Probe
  Componente2 = FC-28 Soil Hygrometer Module
  Componente3 = Arduino Uno (Rev3)

nets:
  N1: Componente1.POS, Componente2.POS
  N2: Componente1.NEG, Componente2.NEG
  VCC: Componente2.VCC, Componente3.5V
  GND: Componente2.GND, Componente3.GND
  N3: Componente2.AO, Componente3.A0

custom parts:
  FC-28 Soil Hygrometer Module - Probe: The FC-28 is a soil hygrometer module that uses the Texas Instruments LM393 comparator chip to provide an analog measurement of soil humidity.
  FC-28 Soil Hygrometer Module: The FC-28 is a soil hygrometer module that uses the Texas Instruments LM393 comparator chip to provide an analog measurement of soil humidity. The digital output is high when soil moisture is over a certain threshold, as determined by adjusting the potentiometer.
