# Fritzing sketch Diagrama de conexión (saved by Fritzing 0.9.3b)
breadboards: 1

parts:
  R1 = Photocell (LDR) [package=THT]
  Componente1 = Arduino Uno (Rev3)
  R2 = Resistor [tolerance=±5% resistance=10k package="0402 [SMD]"]

nets:
  N1: R1.pin_0, Componente1.5V
  N2: R1.pin_1, Componente1.A0, R2.Pin_1
