# Fritzing sketch diagrama_conexión_lm35 (saved by Fritzing 0.9.3b)
breadboards: 1

parts:
  Componente1 = Arduino Uno (Rev3)
  T1 = LM35 Temperature Sensor [package="TO92 [THT]"]

nets:
  N1: Componente1.A5/SCL, T1.Vout
  N2: Componente1.5V, T1.+Vs
  GND: Componente1.GND, T1.GND
