# Fritzing sketch diagrama_catodo (saved by Fritzing 0.9.3b)
breadboards: 1

parts:
  LED1 = RGB LED (com. cathode, rgb) [package="5 mm [THT]"]
  R1 = Resistor [tolerance=±5% resistance=220 package=THT]
  Componente1 = Arduino Uno (Rev3) - ICSP
  R2 = Resistor [tolerance=±5% resistance=220 package=THT]
  R3 = Resistor [tolerance=±5% resistance=220 package=THT]

nets:
  N1: LED1.red_anode, R3.Pin_1
  N2: LED1.common_cathode, Componente1.GND
  N3: LED1.green_anode, R2.Pin_1
  N4: LED1.blue_anode, R1.Pin_1
  N5: R1.Pin_0, Componente1.D11_PWM/MOSI
  N6: Componente1.D9_PWM, R3.Pin_0
  N7: Componente1.D10_PWM/SS, R2.Pin_0
