# Fritzing sketch pinza (saved by Fritzing 0.9.3b)
breadboards: 1

parts:
  J1 = Basic Servo
  Componente1 = Arduino Uno (Rev3) - ICSP
  J2 = Basic Servo
  J3 = Basic Servo

nets:
  GND: J1.gnd, J2.gnd, J3.gnd
  VCC: J1.vcc, J2.vcc, J3.vcc
  N1: J1.pulse, Componente1.D6_PWM
  N2: Componente1.D3_PWM, J3.pulse
  N3: Componente1.D5_PWM, J2.pulse

notes:
  BASE - PIN DIGITAL 3
  CENTRO - PIN DIGITAL 5
  PINZA - PIN DIGITAL 6
