# Fritzing sketch diseno_conexion (saved by Fritzing 0.9.3b)
breadboards: 1

parts:
  R1 = Photocell (LDR) [package=THT]
  VCC1 = Battery block 9V
  Display1 = LCD screen 16x2 IIC [part_number=101290]
  Componente1 = DHT22 module
  R2 = Rotary Potentiometer (Small) [maximum_resistance=100kΩ package=THT]
  Componente2 = Arduino Nano (Rev3.0)
  Componente3 = FC-28 Soil Hygrometer Module - Probe
  Componente4 = FC-28 Soil Hygrometer Module
  R3 = Resistor [tolerance=±5% resistance=220 package=THT]

nets:
  VCC: R1.pin_0, Display1.VCC, Componente1.VCC, R2.leg1, Componente2.5V, Componente4.VCC
  GND: R1.pin_1, VCC1.-, Display1.GND, Componente1.GND, R2.leg2, Componente2.GND, Componente4.GND, R3.Pin_0
  N1: VCC1.+, Componente2.VIN
  N2: Display1.SDA, Componente2.A4
  N3: Display1.SCL, Componente2.A5
  N4: Componente1.DATA, Componente2.D2
  N5: R2.wiper, Componente2.A1
  N6: Componente2.A2, R3.Pin_1
  N7: Componente2.A0, Componente4.AO
  N8: Componente3.POS, Componente4.POS
  N9: Componente3.NEG, Componente4.NEG

notes:
  Pin de conexión (2)
  Pin de conexión (A0)
  Pines de conexión: SDA: A4 , SCL: A5
  Pin de conexión A1
  Pin de conexión A2

custom parts:
  LCD screen 16x2 IIC: LCD screen with HD44780 controller enables showing text, symbols, value or anything else that comes from Croduino/Arduino. It is capable of showing 16 symbols in two lines and therefore can be used in many projects that need to send clearly visible and legible output information.. • Color of symbols: White • Backlight: Blue • Dimensions: 80 x 36 x 12 mm • Screen dimensions: 64.5 x 16 mm •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
  FC-28 Soil Hygrometer Module - Probe: The FC-28 is a soil hygrometer module that uses the Texas Instruments LM393 comparator chip to provide an analog measurement of soil humidity.
  FC-28 Soil Hygrometer Module: The FC-28 is a soil hygrometer module that uses the Texas Instruments LM393 comparator chip to provide an analog measurement of soil humidity. The digital output is high when soil moisture is over a certain threshold, as determined by adjusting the potentiometer.
