# Fritzing sketch Untitled Sketch 2 (saved by Fritzing 0.9.3b)
breadboards: 1

parts:
  A1 = 2 channel relay module [package=THT]
  VALVE1 = Plastic Solenoid Valve
  VCC1 = Battery block 9V
  VALVE2 = Plastic Solenoid Valve
  Componente1 = Arduino Uno (Rev3) - ICSP

nets:
  N1: A1.pin_1, VALVE1.no_name_yet#1
  N2: A1.pin_2, VCC1.+
  N3: A1.pin_4, VALVE2.no_name_yet#1
  N4: VALVE1.no_name_yet#2, VCC1.-, VALVE2.no_name_yet#2, Componente1.GND

custom parts:
  2 channel relay module: 2 channel Relay Module 5V 12V 24V High and Low Level Trigger Relay Control With Optocoupler Two Way relays DC 5 V 12 V 24 V Volt.
