# Fritzing sketch Esquema básico (saved by Fritzing 0.9.3b)

parts:
  Componente1 = 4x4 Keypad [part_number=101207]
  Componente2 = Arduino Uno (Rev3)

nets:
  N1: Componente1.1, Componente2.D11_PWM/MOSI
  N2: Componente1.2, Componente2.D10_PWM/SS
  N3: Componente1.3, Componente2.D9_PWM
  N4: Componente1.4, Componente2.D8
  N5: Componente1.5, Componente2.D7
  N6: Componente1.6, Componente2.D6_PWM
  N7: Componente1.7, Componente2.D5_PWM
  N8: Componente1.8, Componente2.D4

notes:
  FILAS
  1F -> 11
  2F -> 10
  3F -> 9
  4F ->8
  COLUMNAS
  5C -> 7
  6C -> 6
  7C -> 5
  8C -> 4

custom parts:
  4x4 Keypad: Matrix membrane keypad 4x4
