# Fritzing sketch diagram_lect_pul (saved by Fritzing 0.9.3b)
breadboards: 1

parts:
  S1 = Pushbutton [package="[THT]"]
  Componente1 = Arduino Uno (Rev3) - ICSP
  R1 = Resistor [tolerance=±5% resistance=220 package=THT]
  LED1 = smd LED [color="Red (633nm)" package="0603 [SMD]"]

nets:
  N1: S1.Pin_1, S1.Pin_2, Componente1.D2, R1.Pin_0
  N2: S1.Pin_3, S1.Pin_4, Componente1.5V
  N3: Componente1.D13/SCK, LED1.anode
  N4: Componente1.GND, R1.Pin_1, LED1.cathode
