# Fritzing sketch diagram_led (saved by Fritzing 0.9.3b)
breadboards: 1

parts:
  LED1 = smd LED [color="Red (633nm)" package="0805 [SMD]"]
  R1 = Resistor [tolerance=±5% resistance=220 package="2512 [SMD]"]
  Componente1 = Arduino Uno (Rev3)

nets:
  N1: LED1.cathode, R1.Pin_1
  N2: LED1.anode, Componente1.D13/SCK
  N3: R1.Pin_0, Componente1.GND
