# Fritzing sketch diagrama_led_serie (saved by Fritzing 0.9.3b)
breadboards: 1

parts:
  Componente1 = Arduino Uno (Rev3) - ICSP
  LED1 = smd LED [color="Red (633nm)" package="0603 [SMD]"]
  R1 = Resistor [tolerance=±5% resistance=220 package="2512 [SMD]"]

nets:
  N1: Componente1.D3_PWM, LED1.anode
  N2: Componente1.GND, R1.Pin_0
  N3: LED1.cathode, R1.Pin_1
