# Fritzing sketch diagram_l298n (saved by Fritzing 0.9.3b)

parts:
  S1 = H-Bridge with L298N
  Componente1 = Arduino Uno (Rev3)
  M2 = DC Motor
  VCC1 = Battery block 9V
  M1 = DC Motor

nets:
  12V: S1.12V, Componente1.5V, VCC1.+
  N1: S1.GND, VCC1.-
  N2: S1.ENA, Componente1.D10_PWM/SS
  N3: S1.IN1, Componente1.D9_PWM
  N4: S1.IN2, Componente1.D8
  N5: S1.IN3, Componente1.D7
  N6: S1.IN4, Componente1.D6_PWM
  N7: S1.ENB, Componente1.D5_PWM
  N8: S1.M1-01, M1.pin_2
  N9: S1.M1-02, M1.pin_1
  N10: S1.M2-01, M2.pin_2
  N11: S1.M2-02, M2.pin_1

custom parts:
  H-Bridge with L298N: h-bridge
