# Fritzing sketch diagrama (saved by Fritzing 0.9.3b)
breadboards: 1

parts:
  S1 = Pushbutton [package="[THT]"]
  LED1 = LED - 5mm [color="Red (633nm)" package="5 mm [THT]"]
  LED2 = LED - 5mm [color="Red (633nm)" package="5 mm [THT]"]
  LED3 = LED - 5mm [color="Red (633nm)" package="5 mm [THT]"]
  Componente1 = Arduino Uno (Rev3) - ICSP
  Componente2 = 4x4 Keypad [part_number=101207]
  R1 = Resistor [tolerance=±5% resistance=220 package=THT]
  R2 = Resistor [tolerance=±5% resistance=220 package=THT]
  R3 = Resistor [tolerance=±5% resistance=220 package=THT]
  R4 = Resistor [tolerance=±5% resistance=220 package=THT]
  J1 = Basic Servo

nets:
  N1: S1.Pin_1, S1.Pin_2, Componente1.D13/SCK, R4.Pin_0
  5V: S1.Pin_3, S1.Pin_4, Componente1.5V, J1.vcc
  N2: LED1.cathode, R1.Pin_0
  N3: LED1.anode, Componente1.D12/MISO
  N4: LED2.cathode, R2.Pin_0
  N5: LED2.anode, Componente1.D11_PWM/MOSI
  N6: LED3.cathode, R3.Pin_0
  N7: LED3.anode, Componente1.D10_PWM/SS
  N8: Componente1.A0, J1.pulse
  N9: Componente1.D8, Componente2.7
  N10: Componente1.D9_PWM, Componente2.8
  N11: Componente1.D2, Componente2.1
  N12: Componente1.D3_PWM, Componente2.2
  N13: Componente1.D4, Componente2.3
  N14: Componente1.D5_PWM, Componente2.4
  N15: Componente1.D6_PWM, Componente2.5
  N16: Componente1.D7, Componente2.6
  GND: Componente1.GND, R1.Pin_1, R2.Pin_1, R3.Pin_1, R4.Pin_1, J1.gnd

custom parts:
  4x4 Keypad: Matrix membrane keypad 4x4
